# Fritzing sketch Marcios teclado (saved by Fritzing 0.7.7b)
breadboards: 1

parts:
  Q1 = NPN-Transistor [package="TO92 [THT]"]
  Q2 = NPN-Transistor [package="TO92 [THT]"]
  Q3 = NPN-Transistor [package="TO92 [THT]"]
  Q4 = NPN-Transistor [package="TO92 [THT]"]
  R1 = Resistor [tolerance=±5% resistance=10k package=THT]
  R2 = Resistor [tolerance=±5% resistance=10k package=THT]
  R3 = Resistor [tolerance=±5% resistance=10k package=THT]
  Interface = mystery part, 5 pins [chip_label=?]
  Key1 = mystery part, 2 pins [chip_label=?]
  Key2 = mystery part, 2 pins [chip_label=?]
  Key3 = mystery part, 2 pins [chip_label=?]
  Key4 = mystery part, 2 pins [chip_label=?]
  Key5 = mystery part, 2 pins [chip_label=?]
  R4 = Resistor [tolerance=±5% resistance=10k package=THT]
  R5 = Resistor [tolerance=±5% resistance=10k package=THT]
  part = NPN-Transistor [package="TO92 [THT]"]

nets:
  N1: Q1.E, Key1.pin1
  N2: Q1.B, R1.Pin_0
  N3: Q1.C, Key1.pin2
  N4: Q2.E, Key2.pin1
  N5: Q2.B, R2.Pin_0
  N6: Q2.C, Key2.pin2
  N7: Q3.E, Key3.pin1
  N8: Q3.B, R3.Pin_0
  N9: Q3.C, Key3.pin2
  N10: Q4.E, Key4.pin1
  N11: Q4.B, R4.Pin_0
  N12: Q4.C, Key4.pin2
  N13: R1.Pin_1, Interface.pin5
  N14: R2.Pin_1, Interface.pin4
  N15: R3.Pin_1, Interface.pin3
  N16: Interface.pin1, R5.Pin_1
  N17: Interface.pin2, R4.Pin_1
  N18: Key5.pin1, part.E
  N19: Key5.pin2, part.C
  N20: R5.Pin_0, part.B
