# Fritzing sketch arduino_alone_PCB (saved by Fritzing 0.7.7b)
breadboards: 1

parts:
  Atmega_88/168/328 = atmega168 [package=dip]
  VCC = Battery
  XTAL = Crystal [frequency="16 Mhz" package=THT]
  22pF = Ceramic Capacitor [capacitance=100nF package="100 mil [THT, multilayer]"]
  22pF_2 = Ceramic Capacitor [capacitance=100nF package="100 mil [THT, multilayer]"]
  A0_-_A5 = mystery part, 6 pins [chip_label=? spacing=300mil]
  7805 = Voltage Regulator - 5V [package="TO220 [THT]"]
  D0-D4 = mystery part, 5 pins [chip_label=? spacing=300mil]
  D5-D8 = mystery part, 4 pins [chip_label=? spacing=300mil]
  D9-D13 = mystery part, 5 pins [chip_label=? spacing=300mil]
  - = mystery part, 4 pins [chip_label=? spacing=300mil]
  LED-ON = LED - 3mm [color="Red (633nm)" package="3 mm [THT]"]
  100R = Resistor [tolerance=±5% resistance=220 package=THT]
  LED13 = LED - 3mm [color="Red (633nm)" package="3 mm [THT]"]
  100R_2 = Resistor [tolerance=±5% resistance=220 package=THT]

nets:
  N1: Atmega_88/168/328.D0_(RX), D0-D4.pin1
  N2: Atmega_88/168/328.D1_(TX), D0-D4.pin2
  N3: Atmega_88/168/328.D2, D0-D4.pin3
  N4: Atmega_88/168/328.D3_(PWM), D0-D4.pin4
  N5: Atmega_88/168/328.D4, D0-D4.pin5
  N6: Atmega_88/168/328.VCC, Atmega_88/168/328.AVCC, 7805.output_voltage, -.pin3, -.pin4, 100R.Pin_0
  GND: Atmega_88/168/328.GND, VCC.+, 22pF.1, 22pF_2.1, 7805.GND, -.pin1, -.pin2, LED-ON.cathode, LED13.cathode
  N7: Atmega_88/168/328.XLAT1, XTAL.pin_0, 22pF.0
  N8: Atmega_88/168/328.XLAT2, XTAL.pin_1, 22pF_2.0
  N9: Atmega_88/168/328.D5_(PWM), D5-D8.pin4
  N10: Atmega_88/168/328.D6_(PWM), D5-D8.pin3
  N11: Atmega_88/168/328.D7, D5-D8.pin2
  N12: Atmega_88/168/328.D8, D5-D8.pin1
  N13: Atmega_88/168/328.D9_(PWM), D9-D13.pin5
  N14: Atmega_88/168/328.D10_(PWM), D9-D13.pin4
  N15: Atmega_88/168/328.D11_(PWM), D9-D13.pin3
  N16: Atmega_88/168/328.D12, D9-D13.pin2
  N17: Atmega_88/168/328.D13, D9-D13.pin1, 100R_2.Pin_0
  N18: Atmega_88/168/328.A0, A0_-_A5.pin6
  N19: Atmega_88/168/328.A1, A0_-_A5.pin5
  N20: Atmega_88/168/328.A2, A0_-_A5.pin4
  N21: Atmega_88/168/328.A3, A0_-_A5.pin3
  N22: Atmega_88/168/328.A4, A0_-_A5.pin2
  N23: Atmega_88/168/328.A5, A0_-_A5.pin1
  N24: VCC.-, 7805.input_voltage
  N25: LED-ON.anode, 100R.Pin_1
  N26: LED13.anode, 100R_2.Pin_1

notes:
  +
  -
