# Fritzing sketch motor_L293d (saved by Fritzing 0.7.5b)
breadboards: 1

parts:
  IC1 = L293D [package=THT]
  In1 = mystery part, 3 pins [chip_label=? spacing=300mil]
  M1 = mystery part, 2 pins [chip_label=? spacing=300mil]
  Bat+ = mystery part, 2 pins [chip_label=? spacing=300mil]
  In2 = mystery part, 3 pins [chip_label=? spacing=300mil]
  M2 = mystery part, 2 pins [chip_label=? spacing=300mil]
  5v = mystery part, 2 pins [chip_label=? spacing=300mil]

nets:
  N1: IC1.Enable_1, In1.pin1
  N2: IC1.In_1, In1.pin2
  N3: IC1.Out_1_(_Controlled_by_Enable_1_), M1.pin1
  N4: IC1.0V, Bat+.pin2, 5v.pin1
  N5: IC1.Out_2_(_Controlled_by_Enable_1_), M1.pin2
  N6: IC1.In_2, In1.pin3
  N7: IC1.+Vmotor, Bat+.pin1
  N8: IC1.Enable_2, In2.pin3
  N9: IC1.In_3, In2.pin2
  N10: IC1.Out_3_(_Controlled_by_Enable_2_), M2.pin2
  N11: IC1.Out_4_(_Controlled_by_Enable_2_), M2.pin1
  N12: IC1.In_4, In2.pin1
  N13: IC1.+V, 5v.pin2

notes:
  TechWeek UNIFEV
  Robotica/Arduino
  E
  +
  1
  -
  M2
  M1
  5v
  bat
